# Fritzing sketch sunnyday_hackathon_4 (saved by Fritzing 0.9.3b)

parts:
  부품1 = Arduino Uno (Rev3) - ICSP
  Part1 = KY-015 Temperature & Humidity Sensor Module [package="Breakout board"]
  ESP1 = ESP32-DevkitC
  S1 = H-Bridge with L298N
  BAT1 = BC9VPC [package=bc9vpc]
  U1 = LIPO-2000mAh [package=lipo-2000]
  부품2 = Adafruit I2C+SPI LCD Backpack [part_number="Adafruit #292"]
  M1 = DC Motor
  M2 = DC Motor
  M3 = DC Motor
  M4 = DC Motor
  U2 = LCD-16X2 [package=lcd-16x2]

nets:
  N1: 부품1.A4/SDA, 부품2.CLOCK
  N2: 부품1.A5/SCL, 부품2.DATA
  N3: 부품1.D8, Part1.Vin, ESP1.IO27
  N4: 부품1.D9_PWM, S1.ENA
  N5: 부품1.D6_PWM, S1.IN2
  N6: 부품1.D7, S1.IN1
  5V: 부품1.5V, 부품2.VCC, U2.VDD, U2.A
  GND: 부품1.GND, U1.-, 부품2.GND, U2.VSS, U2.R_W
  N7: 부품1.VIN, U1.+
  N8: Part1.S, ESP1.5V
  N9: Part1.-, ESP1.GND
  N10: S1.12V, BAT1.V+
  N11: S1.GND, BAT1.V-
  N12: S1.M1-01, M1.pin_2, M4.pin_2
  N13: S1.M1-02, M1.pin_1, M4.pin_1
  N14: S1.M2-01, M2.pin_2, M3.pin_2
  N15: S1.M2-02, M2.pin_1, M3.pin_1
  N16: 부품2.CONTRAST, U2.VO
  N17: 부품2.RS, U2.RS
  N18: 부품2.E, U2.E
  N19: 부품2.DB0, U2.DB0
  N20: 부품2.DB1, U2.DB1
  N21: 부품2.DB2, U2.DB2
  N22: 부품2.DB3, U2.DB3
  N23: 부품2.DB4, U2.DB4
  N24: 부품2.DB5, U2.DB5
  N25: 부품2.DB6, U2.DB6
  N26: 부품2.DB7, U2.DB7
  N27: 부품2.LEDK, U2.K

custom parts:
  KY-015 Temperature & Humidity Sensor Module: KY-015 temperature and humidity sensor module, provides a low-latency serial interface to measure humidity and temperature.
  H-Bridge with L298N: h-bridge
  Adafruit I2C+SPI LCD Backpack: LCD backpacks reduce the number of pins needed to connect to an LCD. LCDs are a fun and easy way to have your microcontroller project talk back to you. Character LCDs are common, and easy to get, available in tons of colors and sizes. We've written tutorials on using character LCDs with an Arduino (or similar microcontroller) but find that the number of pins necessary to control the LCD can be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
